# Fritzing sketch sonar (saved by Fritzing 0.9.3b)
circuit board: 8.46667cm x 5.64444cm

parts:
  Part1 = Arduino Uno (Rev3)
  hc-sr1 = hc-sr04

nets:
  N1: Part1.A0, hc-sr1.Trig, hc-sr1.Echo
  GND: Part1.GND, hc-sr1.GND
  5V: Part1.5V, hc-sr1.VCC
