# Fritzing sketch sketch (saved by Fritzing 0.9.3b)

parts:
  Part1 = Arduino Uno (Rev3)  # not connected
  Part2 = Arduino Pro Mini v13
  U1 = L298 [package=multiwatt15_6400bgheatsink]
  U2 = L298 [package=multiwatt15_6400bgheatsink]

nets:
  N1: Part2.D13/SCK, U2.IN4
  N2: Part2.D12/MISO, U2.IN3
  N3: Part2.D11_PWM/MOSI, U2.ENB
  N4: Part2.D10_PWM/SS, U2.IN2
  N5: Part2.D9_PWM, U2.ENA
  N6: Part2.D8, U2.IN1
  N7: Part2.D7, U1.IN4
  N8: Part2.D6_PWM, U1.ENB
  N9: Part2.D5_PWM, U1.IN3
  N10: Part2.D4, U1.IN2
  N11: Part2.D3_PWM, U1.ENA
  N12: Part2.D2, U1.IN1
